// Logisim project ID.circ as structural Verilog: 1 circuit, main circuit ID
module ID (
  input  [3:0] r1,
  input  [3:0] r2,
  input  [3:0] wd,
  input  [3:0] wr,
  input  regWrite,
  input  clk,
  output [3:0] d1,
  output [3:0] d2
);

  wire and_1_out, and_2_out, and_3_out, and_4_out, and_5_out, decoder_1_out1, decoder_1_out2, decoder_1_out3,
       decoder_1_out4, decoder_1_out5;
  wire [3:0] register_1_q, register_2_q, register_3_q, register_4_q, register_5_q, zero_q;

  Decoder #(.select(3)) decoder_1 (
    .out1(decoder_1_out1), .out2(decoder_1_out2), .out3(decoder_1_out3), .out4(decoder_1_out4),
    .out5(decoder_1_out5), .sel(wr[2:0]), .en(1'b1));  // open: out0, out6, out7
  and and_1 (and_1_out, regWrite, decoder_1_out1);
  and and_2 (and_2_out, regWrite, decoder_1_out2);
  and and_3 (and_3_out, regWrite, decoder_1_out3);
  and and_4 (and_4_out, regWrite, decoder_1_out4);
  and and_5 (and_5_out, regWrite, decoder_1_out5);
  Register #(.width(4)) zero (.D(wd), .en(1'b0), .Q(zero_q), .clk(clk));  // open: clr
  Register #(.width(4)) register_1 (.D(wd), .en(and_1_out), .Q(register_1_q), .clk(clk));  // open: clr
  Register #(.width(4)) register_2 (.D(wd), .en(and_2_out), .Q(register_2_q), .clk(clk));  // open: clr
  Register #(.width(4)) register_3 (.D(wd), .en(and_3_out), .Q(register_3_q), .clk(clk));  // open: clr
  Register #(.width(4)) register_4 (.D(wd), .en(and_4_out), .Q(register_4_q), .clk(clk));  // open: clr
  Register #(.width(4)) register_5 (.D(wd), .en(and_5_out), .Q(register_5_q), .clk(clk));  // open: clr
  Multiplexer #(.select(3), .width(4), .enable("false")) multiplexer_1 (
    .in0(zero_q), .in1(register_1_q), .in2(register_2_q), .in3(register_3_q), .in4(register_4_q),
    .in5(register_5_q), .out(d1), .sel(r1[2:0]));  // open: in6, in7
  Multiplexer #(.select(3), .width(4), .enable("false")) multiplexer_2 (
    .in0(zero_q), .in1(register_1_q), .in2(register_2_q), .in3(register_3_q), .in4(register_4_q),
    .in5(register_5_q), .out(d2), .sel(r2[2:0]));  // open: in6, in7
endmodule
