// Logisim project IF.circ as structural Verilog: 1 circuit, main circuit IF
module IF (
  input  [7:0] i1,
  input  [7:0] jump,
  input  s1,
  input  s0,
  input  en,
  input  clk,
  output [7:0] jump_2,
  output [7:0] PC_1,
  output [3:0] r3_im,
  output [3:0] r2,
  output [3:0] r1,
  output [3:0] op
);

  wire [7:0] multiplexer_1_out, register_1_q;

  Multiplexer #(.select(2), .width(8), .enable("false")) multiplexer_1 (
    .in0(PC_1), .in1(i1), .in2(jump), .in3(jump), .out(multiplexer_1_out), .sel({s1, s0}));
  Register register_1 (.D(multiplexer_1_out), .en(en), .Q(register_1_q), .clk(clk), .clr(1'b0));
  Adder adder_1 (.a(8'h1), .b(register_1_q), .out(PC_1), .cin(1'b0));  // open: cout
  ROM #(.dataWidth(16)) rom_1 (.addr(register_1_q), .data({op, jump_2, r3_im}));  // open: sel

  assign r1 = jump_2[7:4];
  assign r2 = jump_2[3:0];

  // Notes on the sheet:
  //   contents of rom_1 (hex, n*v repeats v):
  //   b66f b023 b032 b041 b058 d232 c243 d324 c432 e520 f530 d344 c432 e521 f541 d432 e522 f552 8130
endmodule
